// Logisim project project.circ as structural Verilog: 6 circuits, main circuit main
module main (
  input  in_1,
  input  in_2,
  input  in_3,
  input  in_4,
  input  in_5,
  input  mode,
  input  Instr_bit3,
  input  Instr_bit2,
  input  Instr_bit1,
  input  in_10,
  input  in_11,
  input  Instr_bit0,
  input  in_13,
  output out_14,
  output out_15,
  output out_16,
  output out_17,
  output negative,
  output zero_status,
  output magnitude,
  output out_21,
  output out_22,
  output out_23,
  output out_24
);

  wire add, add00, add01, add10, add11, add_sub, addr1, and_2_out, and_3_out, and_4_out, and_5_out,
       and_6_out, and_7_out, and_8_out, and_9_out, and_10_out, and_11_out, and_12_out, and_13_out,
       and_14_out, and_15_out, and_17_out, and_18_out, and_20_out, and_21_out, and_22_out, and_23_out,
       and_24_out, and_25_out, and_62_out, and_64_out, and_65_out, and_66_out, and_67_out, and_68_out,
       and_69_out, and_70_out, and_71_out, and_72_out, and_73_out, and_74_out, and_75_out, and_76_out,
       and_77_out, and_78_out, and_79_out, and_80_out, and_81_out, and_82_out, and_83_out, and_84_out,
       and_85_out, and_86_out, and_87_out, and_88_out, and_89_out, AoutR0, AoutR1, clck, clock_1_out,
       data_ram0, data_ram1, data_ram2, data_ram3, ExR0_bit0, ExR0_bit1, ExR0_bit2, ExR0_bit3, ExR1_bit0,
       ExR1_bit1, ExR1_bit2, ExR1_bit3, Halt, Insert_Mode, instruction_ram_1_data_output_bit0,
       instruction_ram_1_data_output_bit1, instruction_ram_1_data_output_bit2,
       instruction_ram_1_data_output_bit3, IR0, IR1, IR2, IR3, Jump, L0, L1, L2, L3, ld, ld01, ld10, ld11,
       load10_bit0, load10_bit1, load10_bit2, load10_bit3, load11_bit0, load11_bit1, load11_bit2,
       load11_bit3, mode_t, not_1_out, not_2_out, not_3_out, not_4_out, not_5_out, not_6_out, not_7_out,
       not_8_out, not_9_out, not_10_out, not_11_out, not_12_out, not_13_out, not_14_out, not_15_out,
       not_16_out, not_17_out, not_18_out, not_19_out, not_20_out, not_21_out, not_22_out, not_23_out,
       not_24_out, not_25_out, not_26_out, not_27_out, or_3_out, or_4_out, or_5_out, or_6_out, or_7_out,
       or_8_out, or_9_out, or_10_out, or_11_out, or_12_out, or_13_out, or_14_out, or_15_out, or_17_out,
       or_18_out, or_19_out, or_21_out, or_22_out, or_23_out, or_24_out, or_25_out, or_28_out, or_29_out,
       or_30_out, or_31_out, or_32_out, or_33_out, or_35_out, or_36_out, or_38_out, or_40_out, or_41_out,
       or_42_out, or_43_out, or_44_out, or_45_out, or_47_out, or_48_out, or_49_out, or_51_out, or_52_out,
       or_53_out, or_54_out, or_56_out, or_57_out, or_58_out, or_60_out, or_61_out, or_62_out, or_63_out,
       or_64_out, or_65_out, or_66_out, or_67_out, or_69_out, or_76_out, or_77_out, or_79_out, or_80_out,
       or_82_out, or_83_out, or_86_out, or_88_out, or_90_out, or_91_out, or_93_out, or_94_out, or_95_out,
       or_96_out, or_98_out, or_99_out, or_100_out, or_101_out, or_102_out, or_104_out, PC0, PC1, PC2,
       PC_bit0_q, PC_bit1_q, PC_bit2_q, PC_Out0, PC_Out1, PC_Out2, procede_jump, R0, R0_0, R0_1, R0_2, R0_3,
       R0_In0, R0_In1, R0_In2, R0_In3, R1, R1_0, R1_1, R1_2, R1_3, R1_In0, R1_In1, R1_In2, R1_In3, R2, R3,
       RAM_in0, RAM_in1, RAM_in2, RAM_in3, Reset_R0_0, Reset_R0_1, Reset_R0_2, Reset_R0_3, Reset_R1_0,
       Reset_R1_1, Reset_R1_2, Reset_R1_3, sub, sub00, sub01, sub10, sv, sv00, sv00_bit0, sv00_bit1,
       sv00_bit2, sv00_bit3, sv01, sv01_bit0, sv01_bit1, sv01_bit2, sv01_bit3, sv10, sv10_bit0, sv10_bit1,
       sv10_bit2, sv10_bit3, sv11, sv11_bit0, sv11_bit1, sv11_bit2, sv11_bit3;

  not not_1 (not_1_out, Halt);
  Clock clock_1 (.out(clock_1_out));
  D_Flip_Flop PC_bit0 (.D(PC0), .clk(clck), .Q(PC_bit0_q));  // open: Qn, preset, reset
  D_Flip_Flop PC_bit1 (.D(PC1), .clk(clck), .Q(PC_bit1_q));  // open: Qn, preset, reset
  D_Flip_Flop PC_bit2 (.D(PC2), .clk(clck), .Q(PC_bit2_q));  // open: Qn, preset, reset
  and and_1 (clck, not_1_out, clock_1_out);
  not not_2 (not_2_out, in_13);
  PC_Incr pc_incr_1 (
    .Clck(clck), .One_Bit(not_2_out), .PC0(PC_bit0_q), .PC1(PC_bit1_q), .PC2(PC_bit2_q), .PC_Out0(PC_Out0),
    .PC_Out1(PC_Out1), .PC_Out2(PC_Out2));
  Instruction_RAM instruction_ram_1 (
    .Clck(clck), .Mode_Input_Pin(mode), .Address_Bit0(PC_bit0_q), .Address_Bit1(PC_bit1_q),
    .Address_Bit2(PC_bit2_q), .Instrct_Input_Bit3(Instr_bit3), .Instrct_Input_Bit2(Instr_bit2),
    .Instrct_Input_Bit1(Instr_bit1), .Instrct_Input_Bit0(Instr_bit0),
    .Data_Output_Bit3(instruction_ram_1_data_output_bit3),
    .Data_Output_Bit2(instruction_ram_1_data_output_bit2),
    .Data_Output_Bit1(instruction_ram_1_data_output_bit1),
    .Data_Output_Bit0(instruction_ram_1_data_output_bit0));
  D_Flip_Flop u_IR3 (.D(instruction_ram_1_data_output_bit3), .clk(clck), .Q(IR3));  // open: Qn, preset, reset
  D_Flip_Flop u_IR2 (.D(instruction_ram_1_data_output_bit2), .clk(clck), .Q(IR2));  // open: Qn, preset, reset
  D_Flip_Flop u_IR1 (.D(instruction_ram_1_data_output_bit1), .clk(clck), .Q(IR1));  // open: Qn, preset, reset
  D_Flip_Flop u_IR0 (.D(instruction_ram_1_data_output_bit0), .clk(clck), .Q(IR0));  // open: Qn, preset, reset
  or or_1 (L3, and_4_out, and_5_out);
  or or_2 (R3, and_2_out, and_3_out);
  or or_3 (or_3_out, add10, or_10_out);
  CU cu_1 (
    .clck(clck), .IR3(IR3), .IR2(IR2), .IR1(IR1), .IR0(IR0), .Mode(mode_t), .ld_R1_0(ld10), .ld_R0_1(ld01),
    .ld_R1_1(ld11), .sv_R0_0(sv00), .sv_R0_1(sv01), .sv_R1_0(sv10), .sv_R1_1(sv11), .add_R0_R0(add00),
    .add_R0_R1(add01), .add_R1_R0(add10), .add_R1_R1(add11), .sub_R0_R0(sub00), .sub_R0_R1(sub01),
    .sub_R1_R0(sub10), .Halt(Halt), .Jump(Jump));
  or or_4 (or_4_out, add00, add01);
  or or_5 (or_5_out, or_4_out, sub00);
  or or_6 (or_6_out, or_5_out, sub01);
  or or_7 (or_7_out, add11, sub10);
  or or_8 (or_8_out, add10, or_7_out);
  or or_9 (or_9_out, add00, sub10);
  or or_10 (or_10_out, or_9_out, sub00);
  and and_2 (and_2_out, or_3_out, R0_3);
  and and_3 (and_3_out, or_11_out, R1_3);
  or or_11 (or_11_out, sub01, or_12_out);
  or or_12 (or_12_out, add11, add01);
  or or_13 (or_13_out, R0_In3, ExR0_bit3);
  or or_14 (or_14_out, add00, add01);
  and and_4 (and_4_out, or_6_out, R0_3);
  and and_5 (and_5_out, or_8_out, R1_3);
  or or_15 (or_15_out, add10, or_24_out);
  or or_16 (R2, and_6_out, and_9_out);
  or or_17 (or_17_out, R1_In3, ExR1_bit3);
  or or_18 (or_18_out, or_14_out, add11);
  or or_19 (or_19_out, sub00, sub01);
  or or_20 (L2, and_10_out, and_8_out);
  or or_21 (or_21_out, add11, sub10);
  or or_22 (or_22_out, add10, or_21_out);
  or or_23 (or_23_out, add00, sub10);
  or or_24 (or_24_out, or_23_out, sub00);
  and and_6 (and_6_out, or_15_out, R0_2);
  or or_25 (or_25_out, R0_In2, ExR0_bit2);
  S_R_Flip_Flop s_r_ff_1 (.S(or_13_out), .R(Reset_R0_3), .clk(clck), .Q(R0_3));  // open: reset, Qn, preset
  S_R_Flip_Flop s_r_ff_2 (.S(or_17_out), .R(Reset_R1_3), .clk(clck), .Q(R1_3));  // open: reset, Qn, preset
  and and_7 (and_7_out, not_3_out, PC_Out2);
  not not_3 (not_3_out, procede_jump);
  or or_26 (add, or_18_out, add10);
  or or_27 (sub, or_19_out, sub10);
  or or_28 (or_28_out, add00, add01);
  or or_29 (or_29_out, or_28_out, sub00);
  or or_30 (or_30_out, or_29_out, sub01);
  and and_8 (and_8_out, or_22_out, R1_2);
  and and_9 (and_9_out, or_31_out, R1_2);
  or or_31 (or_31_out, sub01, or_32_out);
  or or_32 (or_32_out, add11, add01);
  S_R_Flip_Flop s_r_ff_3 (.S(or_25_out), .R(Reset_R0_2), .clk(clck), .Q(R0_2));  // open: reset, Qn, preset
  S_R_Flip_Flop s_r_ff_4 (.S(or_33_out), .R(Reset_R1_2), .clk(clck), .Q(R1_2));  // open: reset, Qn, preset
  or or_33 (or_33_out, R1_In2, ExR1_bit2);
  or or_34 (PC2, and_7_out, and_20_out);
  and and_10 (and_10_out, or_30_out, R0_2);
  or or_35 (or_35_out, add00, sub10);
  or or_36 (or_36_out, add10, or_42_out);
  or or_37 (R1, and_13_out, and_14_out);
  and and_11 (and_11_out, not_4_out, PC_Out1);
  not not_4 (not_4_out, procede_jump);
  not not_5 (not_5_out, add);
  or or_38 (or_38_out, add00, add01);
  or or_39 (L1, and_17_out, and_12_out);
  or or_40 (or_40_out, add11, sub10);
  or or_41 (or_41_out, add10, or_40_out);
  and and_12 (and_12_out, or_41_out, R1_1);
  or or_42 (or_42_out, or_35_out, sub00);
  and and_13 (and_13_out, or_36_out, R0_1);
  and and_14 (and_14_out, or_43_out, R1_1);
  or or_43 (or_43_out, sub01, or_44_out);
  or or_44 (or_44_out, add11, add01);
  S_R_Flip_Flop s_r_ff_5 (.S(or_51_out), .R(Reset_R0_1), .clk(clck), .Q(R0_1));  // open: reset, Qn, preset
  S_R_Flip_Flop s_r_ff_6 (.S(or_45_out), .R(Reset_R1_1), .clk(clck), .Q(R1_1));  // open: reset, Qn, preset
  or or_45 (or_45_out, R1_In1, ExR1_bit1);
  or or_46 (PC1, and_11_out, and_24_out);
  and and_15 (and_15_out, not_6_out, PC_Out0);
  not not_6 (not_6_out, procede_jump);
  and and_16 (add_sub, not_5_out, sub);
  or or_47 (or_47_out, or_38_out, sub00);
  or or_48 (or_48_out, or_47_out, sub01);
  and and_17 (and_17_out, or_48_out, R0_1);
  or or_49 (or_49_out, add10, or_53_out);
  or or_50 (R0, and_18_out, and_22_out);
  or or_51 (or_51_out, R0_In1, ExR0_bit1);
  or or_52 (or_52_out, add00, sub10);
  or or_53 (or_53_out, or_52_out, sub00);
  and and_18 (and_18_out, or_49_out, R0_0);
  S_R_Flip_Flop s_r_ff_7 (.S(or_64_out), .R(Reset_R0_0), .clk(clck), .Q(R0_0));  // open: reset, Qn, preset
  S_R_Flip_Flop s_r_ff_8 (.S(or_54_out), .R(Reset_R1_0), .clk(clck), .Q(R1_0));  // open: reset, Qn, preset
  or or_54 (or_54_out, R1_In0, ExR1_bit0);
  and and_19 (procede_jump, Jump, mode);
  or or_55 (PC0, and_15_out, and_25_out);
  and and_20 (and_20_out, procede_jump, R0_2);
  or or_56 (or_56_out, add00, add01);
  or or_57 (or_57_out, or_56_out, sub00);
  or or_58 (or_58_out, or_57_out, sub01);
  or or_59 (L0, and_23_out, and_21_out);
  or or_60 (or_60_out, add11, sub10);
  or or_61 (or_61_out, add10, or_60_out);
  and and_21 (and_21_out, or_61_out, R1_0);
  and and_22 (and_22_out, or_62_out, R1_0);
  or or_62 (or_62_out, sub01, or_63_out);
  or or_63 (or_63_out, add11, add01);
  or or_64 (or_64_out, R0_In0, ExR0_bit0);
  and and_23 (and_23_out, or_58_out, R0_0);
  and and_24 (and_24_out, procede_jump, R0_1);
  and and_25 (and_25_out, procede_jump, R0_0);
  or or_65 (or_65_out, sv00_bit2, sv10_bit2);
  or or_66 (or_66_out, sv00_bit1, sv10_bit1);
  or or_67 (or_67_out, sv00_bit0, sv10_bit0);
  or or_68 (R1_In3, load10_bit3, load11_bit3);
  or or_69 (or_69_out, sv00_bit3, sv10_bit3);
  or or_70 (data_ram2, or_65_out, or_76_out);
  or or_71 (data_ram1, or_66_out, or_77_out);
  ALU alu_1 (
    .clck(clck), .L_Input3(L3), .L_Input2(L2), .L_Input1(L1), .L_Input0(L0), .R_Input3(R3), .R_Input2(R2),
    .R_Input1(R1), .R_Input0(R0), .Add_Sub(add_sub), .Negative_Status_Output1_Bit0(negative),
    .Zero_Status_Output2_Bit1(zero_status), .Magnitude_Overflow_Status_Output3_Bit2(magnitude),
    .A_Output3(out_14), .A_Output2(out_15), .A_Output1(out_16), .A_Output0(out_17));
  or or_72 (R1_In2, load10_bit2, load11_bit2);
  or or_73 (R1_In1, load10_bit1, load11_bit1);
  or or_74 (R1_In0, load10_bit0, load11_bit0);
  or or_75 (data_ram3, or_69_out, or_79_out);
  or or_76 (or_76_out, sv01_bit2, sv11_bit2);
  or or_77 (or_77_out, sv01_bit1, sv11_bit1);
  or or_78 (data_ram0, or_67_out, or_80_out);
  or or_79 (or_79_out, sv01_bit3, sv11_bit3);
  or or_80 (or_80_out, sv01_bit0, sv11_bit0);
  and and_26 (R0_In3, ld01, out_21);
  and and_27 (load10_bit3, out_21, ld10);
  and and_28 (load11_bit3, out_21, ld11);
  and and_29 (sv00_bit3, sv00, out_21);
  and and_30 (sv01_bit3, out_21, sv01);
  and and_31 (sv10_bit3, out_21, sv10);
  and and_32 (sv11_bit3, out_21, sv11);
  and and_33 (R0_In2, ld01, out_22);
  and and_34 (load10_bit2, out_22, ld10);
  and and_35 (load11_bit2, out_22, ld11);
  and and_36 (ExR0_bit3, AoutR0, out_14);
  and and_37 (ExR1_bit3, AoutR1, out_14);
  and and_38 (sv00_bit2, sv00, out_22);
  and and_39 (sv01_bit2, out_22, sv01);
  and and_40 (sv10_bit2, out_22, sv10);
  and and_41 (sv11_bit2, out_22, sv11);
  and and_42 (R0_In1, ld01, out_23);
  and and_43 (load10_bit1, out_23, ld10);
  and and_44 (load11_bit1, out_23, ld11);
  and and_45 (ExR0_bit2, AoutR0, out_15);
  and and_46 (ExR1_bit2, AoutR1, out_15);
  and and_47 (sv00_bit1, sv00, out_23);
  and and_48 (R0_In0, ld01, out_24);
  and and_49 (ExR0_bit1, AoutR0, out_16);
  and and_50 (ExR1_bit1, AoutR1, out_16);
  and and_51 (sv01_bit1, out_23, sv01);
  and and_52 (sv10_bit1, out_23, sv10);
  and and_53 (sv11_bit1, out_23, sv11);
  Data_RAM data_ram_1 (
    .Clck(clck), .Mode_Input_Pin(mode_t), .Address_Bit0(addr1), .Address_Bit1(in_10), .Address_Bit2(in_11),
    .Data_Input_Bit3(RAM_in3), .Data_Input_Bit2(RAM_in2), .Data_Input_Bit1(RAM_in1),
    .Data_Input_Bit0(RAM_in0), .Output_Bit3(out_21), .Output_Bit2(out_22), .Output_Bit1(out_23),
    .Output_Bit0(out_24));
  and and_54 (load10_bit0, out_24, ld10);
  and and_55 (load11_bit0, out_24, ld11);
  and and_56 (sv00_bit0, sv00, out_24);
  and and_57 (sv01_bit0, out_24, sv01);
  and and_58 (sv11_bit0, out_24, sv11);
  and and_59 (ExR0_bit0, AoutR0, out_17);
  and and_60 (ExR1_bit0, AoutR1, out_17);
  and and_61 (sv10_bit0, out_24, sv10);
  not not_7 (not_7_out, ld);
  not not_8 (not_8_out, sv);
  and and_62 (and_62_out, in_2, Insert_Mode);
  and and_63 (Insert_Mode, not_7_out, not_8_out);
  or or_81 (RAM_in3, and_62_out, and_64_out);
  and and_64 (and_64_out, sv, data_ram3);
  or or_82 (or_82_out, add00, add01);
  or or_83 (or_83_out, or_82_out, sub00);
  or or_84 (AoutR0, or_83_out, sub01);
  and and_65 (and_65_out, in_3, Insert_Mode);
  or or_85 (RAM_in2, and_65_out, and_66_out);
  or or_86 (or_86_out, add10, add11);
  and and_66 (and_66_out, sv, data_ram2);
  or or_87 (AoutR1, or_86_out, sub10);
  or or_88 (or_88_out, sv00, sv01);
  or or_89 (sv, or_88_out, or_90_out);
  and and_67 (and_67_out, sv, data_ram1);
  or or_90 (or_90_out, sv10, sv11);
  not not_9 (not_9_out, sv00);
  or or_91 (or_91_out, not_9_out, sv01);
  and and_68 (and_68_out, Insert_Mode, in_4);
  or or_92 (RAM_in1, and_67_out, and_68_out);
  not not_10 (not_10_out, sv10);
  or or_93 (or_93_out, not_10_out, sv11);
  or or_94 (or_94_out, or_91_out, or_93_out);
  not not_11 (not_11_out, ld10);
  or or_95 (or_95_out, ld11, not_11_out);
  and and_69 (and_69_out, sv, or_94_out);
  and and_70 (and_70_out, sv, data_ram0);
  or or_96 (or_96_out, ld01, or_95_out);
  or or_97 (RAM_in0, and_70_out, and_71_out);
  or or_98 (or_98_out, ld10, ld11);
  or or_99 (or_99_out, ld11, ld10);
  and and_71 (and_71_out, Insert_Mode, in_5);
  or or_100 (or_100_out, ld10, ld11);
  or or_101 (or_101_out, ld10, ld11);
  or or_102 (or_102_out, ld10, ld11);
  or or_103 (ld, ld01, or_99_out);
  and and_72 (and_72_out, ld, or_96_out);
  or or_104 (or_104_out, and_72_out, and_69_out);
  not not_12 (not_12_out, R1_In2);
  not not_13 (not_13_out, R1_In1);
  not not_14 (not_14_out, R1_In0);
  not not_15 (not_15_out, ExR1_bit0);
  and and_73 (and_73_out, in_1, Insert_Mode);
  not not_16 (not_16_out, R1_In3);
  not not_17 (not_17_out, ExR1_bit3);
  and and_74 (and_74_out, not_12_out, or_101_out);
  not not_18 (not_18_out, ExR1_bit2);
  and and_75 (and_75_out, not_13_out, or_102_out);
  not not_19 (not_19_out, ExR1_bit1);
  and and_76 (and_76_out, not_14_out, or_98_out);
  and and_77 (and_77_out, not_15_out, AoutR1);
  not not_20 (not_20_out, R0_In3);
  not not_21 (not_21_out, ExR0_bit3);
  not not_22 (not_22_out, R0_In2);
  not not_23 (not_23_out, ExR0_bit2);
  not not_24 (not_24_out, R0_In1);
  not not_25 (not_25_out, ExR0_bit1);
  not not_26 (not_26_out, R0_In0);
  not not_27 (not_27_out, ExR0_bit0);
  or or_105 (addr1, or_104_out, and_73_out);
  and and_78 (and_78_out, not_16_out, or_100_out);
  and and_79 (and_79_out, not_17_out, AoutR1);
  and and_80 (and_80_out, not_18_out, AoutR1);
  and and_81 (and_81_out, not_19_out, AoutR1);
  and and_82 (and_82_out, not_20_out, ld01);
  and and_83 (and_83_out, not_21_out, AoutR0);
  and and_84 (and_84_out, not_22_out, ld01);
  and and_85 (and_85_out, not_23_out, AoutR0);
  and and_86 (and_86_out, not_24_out, ld01);
  and and_87 (and_87_out, not_25_out, AoutR0);
  and and_88 (and_88_out, not_26_out, ld01);
  and and_89 (and_89_out, not_27_out, AoutR0);
  or or_106 (Reset_R1_3, and_78_out, and_79_out);
  or or_107 (Reset_R1_2, and_74_out, and_80_out);
  or or_108 (Reset_R1_1, and_75_out, and_81_out);
  or or_109 (Reset_R1_0, and_76_out, and_77_out);
  or or_110 (Reset_R0_3, and_82_out, and_83_out);
  or or_111 (Reset_R0_2, and_84_out, and_85_out);
  or or_112 (Reset_R0_1, and_86_out, and_87_out);
  or or_113 (Reset_R0_0, and_88_out, and_89_out);

  // Other names for the same wires on the sheet: A0 = out_17; A1 = out_16; A2 = out_15; A3 = out_14;
  //   addr_insert = in_1; data_out0 = out_24; data_out1 = out_23; data_out2 = out_22; data_out3 = out_21; md = mode;
  //   RAM_data_in0 = in_5; RAM_data_in1 = in_4; RAM_data_in2 = in_3; RAM_data_in3 = in_2

  // Notes on the sheet:
  //   Clock
  //   PC
  //   Instructions (before Fetch):
  //   Can write instr only when PC Incr is on
  //   and get executed (i.e. Read mode vs write mode)
  //   4. CPU can start running by fetching first instruction
  //   2. Insert in Instruction RAM desired instr. for a maximum of 8 nibbles.
  //   Please, make sure Instr. RAM mode is 1 before execution
  //   1. Insert in Data RAM desired nibbles in addr0 and addr1 using insert mode (Clock must tick)
  //   3. Change instr. RAM mode to 1 (from 0) for instructions to be read before autotick is enabled
  //   Also note that it might be better to manually tick clock before execution when loading instructions.
  //   User determines mode
  //   To Write: mode = 0
  //   To Read: mode = 1
  //   N.B.: If not all nibbles are loaded, jump instruction (0000) will execute, which might result in infinite loop if Reg. block not loaded.
  //   IR
  //   R0 as Left Op
  //   R1 as Left Op
  //   R0 as Right Op
  //   R1 as Right Op
  //   Reg block never resets
  //   Instruction Fetch
  //   CU
  //   Add/Sub mode
  //   Left Operand
  //   Right Operand
  //   Add/Sub Input (for ALU)
  //   REGISTER BLOCK
  //   Jump Execution
  //   PC Increm procedes
  //   Procede to Jump
  //   ALU Output
  //   Execute
  //   Register Block Input Pins
  //   Write Back Circuit
  //   Load
  //   Save
  //   Write-back (ALU to Reg block)
  //   To insert data in RAM by brute force (i.e. without sv instruction)
  //   Data RAM
  //   N.B.: Bits 1 & 2 of Data Ram address to be kept 0 (as size(RAM) = 2)
  //   pin = 1 for addr1
  //   0 for addr0
  //   Address Pin for insert mode data RAM
  //   Data RAM output
  //   Aout to R0
  //   Possible to insert data in Data RAM
  //   LOAD RAM HERE
  //   RAM Input Determinism
  //   Aout to R1
  //   RAM Address: 1/0
  //   Bit0
  //   R1
  //   Bit3
  //   Bit2
  //   Bit1
  //   R0
  //   Register Block RESET Table
  //   Bit3
  //   Bit2
  //   Bit1
  //   Bit0
endmodule

module Instruction_RAM (
  input  Clck,
  input  Mode_Input_Pin,
  input  Address_Bit0,
  input  Address_Bit1,
  input  Address_Bit2,
  input  Instrct_Input_Bit3,
  input  Instrct_Input_Bit2,
  input  Instrct_Input_Bit1,
  input  Instrct_Input_Bit0,
  output Data_Output_Bit3,
  output Data_Output_Bit2,
  output Data_Output_Bit1,
  output Data_Output_Bit0
);

  wire Addr0_And_Gate_out, Addr1_And_Gate_out, Addr2_And_Gate_out, Addr3_And_Gate_out, Addr4_And_Gate_out,
       Addr4_and_Mode_out, Addr5_And_Gate_out, Addr5_and_Mode_out, Addr6_And_Gate_out, Addr6_and_Mode_out,
       Addr6_READ_out, Addr7_And_Gate_out, Addr7_and_Mode_out, Addr_and_Mode_out, and_1_out, and_2_out,
       and_3_out, and_4_out, and_5_out, and_6_out, and_7_out, and_8_out, and_9_out, and_10_out, and_11_out,
       and_12_out, and_13_out, and_14_out, and_15_out, and_16_out, and_17_out, and_18_out, and_19_out,
       and_20_out, and_21_out, and_22_out, and_23_out, and_24_out, and_25_out, and_26_out, and_27_out,
       and_28_out, and_29_out, and_30_out, and_31_out, and_32_out, and_33_out, and_34_out, and_35_out,
       and_36_out, and_37_out, and_38_out, and_39_out, and_40_out, and_41_out, and_42_out, and_43_out,
       and_44_out, and_45_out, and_46_out, and_47_out, and_48_out, and_49_out, and_50_out, and_51_out,
       and_52_out, and_53_out, and_54_out, and_55_out, and_56_out, and_57_out, and_58_out, and_59_out,
       and_60_out, and_61_out, and_62_out, and_63_out, and_64_out, and_65_out, and_66_out, and_67_out,
       and_68_out, and_69_out, and_70_out, and_71_out, and_72_out, and_73_out, and_74_out, and_75_out,
       and_76_out, and_77_out, and_78_out, and_79_out, and_80_out, and_81_out, and_82_out, and_83_out,
       and_84_out, and_85_out, and_86_out, and_87_out, and_88_out, and_89_out, and_90_out, and_91_out,
       and_92_out, and_93_out, and_94_out, and_95_out, and_96_out, and_97_out, and_98_out, and_99_out,
       and_100_out, and_101_out, and_102_out, and_103_out, Data_And_Gate3_out, Data_And_Gate_out,
       Mode_and_Addr2_out, Mode_Reg_q, Mode_Reg_qn, not_1_out, not_2_out, not_3_out, not_4_out, not_5_out,
       not_6_out, not_7_out, not_8_out, not_9_out, not_10_out, not_11_out, not_12_out, not_13_out,
       not_14_out, not_15_out, not_16_out, not_17_out, not_18_out, not_19_out, not_20_out, not_21_out,
       not_22_out, not_23_out, not_24_out, not_25_out, not_26_out, not_27_out, not_28_out, not_29_out,
       not_30_out, not_31_out, not_32_out, not_33_out, not_34_out, not_35_out, not_36_out, not_37_out,
       not_38_out, not_39_out, not_40_out, not_41_out, not_42_out, not_43_out, not_44_out, not_45_out,
       or_1_out, or_2_out, or_3_out, or_4_out, or_5_out, or_6_out, or_7_out, or_8_out, or_9_out, or_10_out,
       or_11_out, or_12_out, or_13_out, or_14_out, or_15_out, or_16_out, or_17_out, or_18_out, or_19_out,
       or_20_out, or_21_out, or_22_out, or_23_out, or_24_out, or_25_out, or_26_out, or_27_out, or_28_out,
       Read_Addr0_out, Read_Addr1_out, Read_Addr2_bit0_out, Read_Addr2_out, READ_Addr7_BIT0_out,
       READ_Addr7_out, Read_Row3_out, Read_Row4_out, Read_Row5_out, Row0_bit0_q, Row0_bit1_q, Row0_bit2_q,
       Row0_bit3_q, Row1_bit0_q, Row1_bit1_q, Row1_bit2_q, Row1_bit3_q, Row2_bit0_q, Row2_bit1_q,
       Row2_bit2_q, Row2_bit3_q, Row3_bit0_q, Row3_bit1_q, Row3_bit2_q, Row3_bit3_q, Row4_bit0_q,
       Row4_bit1_q, Row4_bit2_q, Row4_bit3_q, Row5_bit0_q, Row5_bit1_q, Row5_bit2_q, Row5_bit3_q,
       Row6_bit0_q, Row6_bit1_q, Row6_bit2_q, Row6_bit3_q, Row7_bit0_q, Row7_bit1_q, Row7_bit2_q,
       Row7_bit3_q, s_r_ff_1_q, s_r_ff_2_q, s_r_ff_3_q, s_r_ff_4_q, s_r_ff_5_q, s_r_ff_5_qn, s_r_ff_6_q,
       s_r_ff_6_qn, s_r_ff_7_q, s_r_ff_7_qn;

  not not_1 (not_1_out, Instrct_Input_Bit3);
  not not_2 (not_2_out, Instrct_Input_Bit2);
  not not_3 (not_3_out, Instrct_Input_Bit1);
  not not_4 (not_4_out, Instrct_Input_Bit0);
  D_Flip_Flop Mode_Reg (.D(Mode_Input_Pin), .clk(Clck), .Q(Mode_Reg_q), .Qn(Mode_Reg_qn));  // open: preset, reset
  S_R_Flip_Flop s_r_ff_1 (
    .S(Instrct_Input_Bit3), .R(not_1_out), .clk(Clck), .Q(s_r_ff_1_q));  // open: reset, Qn, preset
  S_R_Flip_Flop s_r_ff_2 (
    .S(Instrct_Input_Bit2), .R(not_2_out), .clk(Clck), .Q(s_r_ff_2_q));  // open: reset, Qn, preset
  S_R_Flip_Flop s_r_ff_3 (
    .S(Instrct_Input_Bit1), .R(not_3_out), .clk(Clck), .Q(s_r_ff_3_q));  // open: reset, Qn, preset
  S_R_Flip_Flop s_r_ff_4 (
    .S(Instrct_Input_Bit0), .R(not_4_out), .clk(Clck), .Q(s_r_ff_4_q));  // open: reset, Qn, preset
  not not_5 (not_5_out, Address_Bit0);
  not not_6 (not_6_out, Address_Bit1);
  not not_7 (not_7_out, Address_Bit2);
  S_R_Flip_Flop s_r_ff_5 (
    .S(Address_Bit0), .R(not_5_out), .clk(Clck), .Q(s_r_ff_5_q), .Qn(s_r_ff_5_qn));  // open: reset, preset
  S_R_Flip_Flop s_r_ff_6 (
    .S(Address_Bit1), .R(not_6_out), .clk(Clck), .Q(s_r_ff_6_q), .Qn(s_r_ff_6_qn));  // open: reset, preset
  S_R_Flip_Flop s_r_ff_7 (
    .S(Address_Bit2), .R(not_7_out), .clk(Clck), .Q(s_r_ff_7_q), .Qn(s_r_ff_7_qn));  // open: reset, preset
  and and_1 (and_1_out, s_r_ff_5_qn, s_r_ff_6_q);
  not not_8 (not_8_out, s_r_ff_5_qn);
  and and_2 (and_2_out, s_r_ff_5_qn, s_r_ff_6_q);
  and and_3 (and_3_out, s_r_ff_5_qn, s_r_ff_6_qn);
  and Addr6_And_Gate (Addr6_And_Gate_out, and_1_out, s_r_ff_7_q);
  and and_4 (and_4_out, s_r_ff_6_q, not_8_out);
  not not_9 (not_9_out, s_r_ff_5_q);
  not not_10 (not_10_out, s_r_ff_6_q);
  and Addr2_And_Gate (Addr2_And_Gate_out, and_2_out, s_r_ff_7_qn);
  and and_5 (and_5_out, s_r_ff_5_q, s_r_ff_6_qn);
  and Addr7_And_Gate (Addr7_And_Gate_out, and_4_out, s_r_ff_7_q);
  and and_6 (and_6_out, not_9_out, not_10_out);
  not not_11 (not_11_out, s_r_ff_7_q);
  and and_7 (and_7_out, s_r_ff_5_q, not_10_out);
  and and_8 (and_8_out, s_r_ff_5_q, s_r_ff_6_q);
  and Addr4_And_Gate (Addr4_And_Gate_out, and_3_out, s_r_ff_7_q);
  and Addr5_And_Gate (Addr5_And_Gate_out, and_5_out, s_r_ff_7_q);
  and Addr6_and_Mode (Addr6_and_Mode_out, Addr6_And_Gate_out, Mode_Reg_qn);
  and Mode_and_Addr2 (Mode_and_Addr2_out, Addr2_And_Gate_out, Mode_Reg_qn);
  and Addr3_And_Gate (Addr3_And_Gate_out, and_8_out, s_r_ff_7_qn);
  and and_9 (and_9_out, Addr3_And_Gate_out, Mode_Reg_qn);
  and Addr4_and_Mode (Addr4_and_Mode_out, Addr4_And_Gate_out, Mode_Reg_qn);
  and Addr5_and_Mode (Addr5_and_Mode_out, Addr5_And_Gate_out, Mode_Reg_qn);
  and Addr7_and_Mode (Addr7_and_Mode_out, Addr7_And_Gate_out, Mode_Reg_qn);
  and Addr0_And_Gate (Addr0_And_Gate_out, and_6_out, not_11_out);
  and Addr1_And_Gate (Addr1_And_Gate_out, not_11_out, and_7_out);
  and and_10 (and_10_out, Mode_Reg_qn, Addr0_And_Gate_out);
  and Addr_and_Mode (Addr_and_Mode_out, Addr1_And_Gate_out, Mode_Reg_qn);
  and Data_And_Gate (Data_And_Gate_out, Mode_and_Addr2_out, s_r_ff_1_q);
  not not_12 (not_12_out, s_r_ff_1_q);
  not not_13 (not_13_out, s_r_ff_1_q);
  not not_14 (not_14_out, s_r_ff_1_q);
  not not_15 (not_15_out, s_r_ff_1_q);
  not not_16 (not_16_out, s_r_ff_1_q);
  S_R_Flip_Flop Row0_bit3 (.S(and_11_out), .R(and_20_out), .clk(Clck), .Q(Row0_bit3_q));  // open: reset, Qn, preset
  and and_11 (and_11_out, and_10_out, s_r_ff_1_q);
  not not_17 (not_17_out, s_r_ff_1_q);
  S_R_Flip_Flop Row1_bit3 (.S(and_12_out), .R(and_23_out), .clk(Clck), .Q(Row1_bit3_q));  // open: reset, Qn, preset
  and and_12 (and_12_out, Addr_and_Mode_out, s_r_ff_1_q);
  not not_18 (not_18_out, s_r_ff_1_q);
  and and_13 (and_13_out, Mode_and_Addr2_out, not_12_out);
  not not_19 (not_19_out, s_r_ff_2_q);
  and Data_And_Gate3 (Data_And_Gate3_out, and_9_out, s_r_ff_1_q);
  not not_20 (not_20_out, s_r_ff_1_q);
  and and_14 (and_14_out, Addr4_and_Mode_out, not_13_out);
  and and_15 (and_15_out, Addr5_and_Mode_out, s_r_ff_1_q);
  and and_16 (and_16_out, Addr5_and_Mode_out, not_14_out);
  and and_17 (and_17_out, Addr6_and_Mode_out, s_r_ff_1_q);
  and and_18 (and_18_out, s_r_ff_1_q, Addr7_and_Mode_out);
  and and_19 (and_19_out, Addr7_and_Mode_out, not_16_out);
  and and_20 (and_20_out, and_10_out, not_17_out);
  and and_21 (and_21_out, and_10_out, s_r_ff_2_q);
  not not_21 (not_21_out, s_r_ff_2_q);
  and and_22 (and_22_out, and_10_out, s_r_ff_3_q);
  and and_23 (and_23_out, Addr_and_Mode_out, not_18_out);
  not not_22 (not_22_out, Mode_Reg_qn);
  S_R_Flip_Flop Row2_bit3 (
    .S(Data_And_Gate_out), .R(and_13_out), .clk(Clck), .Q(Row2_bit3_q));  // open: reset, Qn, preset
  S_R_Flip_Flop Row3_bit3 (
    .S(Data_And_Gate3_out), .R(and_24_out), .clk(Clck), .Q(Row3_bit3_q));  // open: reset, Qn, preset
  and and_24 (and_24_out, and_9_out, not_20_out);
  and and_25 (and_25_out, Addr6_and_Mode_out, not_15_out);
  S_R_Flip_Flop Row0_bit2 (.S(and_21_out), .R(and_26_out), .clk(Clck), .Q(Row0_bit2_q));  // open: reset, Qn, preset
  and and_26 (and_26_out, and_10_out, not_21_out);
  and Read_Addr1 (Read_Addr1_out, Addr1_And_Gate_out, Mode_Reg_q);
  S_R_Flip_Flop Row1_bit2 (.S(and_32_out), .R(and_42_out), .clk(Clck), .Q(Row1_bit2_q));  // open: reset, Qn, preset
  and and_27 (and_27_out, Addr1_And_Gate_out, Mode_Reg_qn);
  and Read_Addr2 (Read_Addr2_out, Addr2_And_Gate_out, not_22_out);
  and and_28 (and_28_out, Mode_and_Addr2_out, s_r_ff_2_q);
  and and_29 (and_29_out, Mode_and_Addr2_out, not_19_out);
  and and_30 (and_30_out, and_9_out, s_r_ff_2_q);
  not not_23 (not_23_out, s_r_ff_2_q);
  S_R_Flip_Flop Row4_bit3 (.S(and_45_out), .R(and_14_out), .clk(Clck), .Q(Row4_bit3_q));  // open: reset, Qn, preset
  S_R_Flip_Flop Row5_bit3 (.S(and_15_out), .R(and_16_out), .clk(Clck), .Q(Row5_bit3_q));  // open: reset, Qn, preset
  S_R_Flip_Flop Row6_bit3 (.S(and_17_out), .R(and_25_out), .clk(Clck), .Q(Row6_bit3_q));  // open: reset, Qn, preset
  S_R_Flip_Flop Row7_bit3 (.S(and_18_out), .R(and_19_out), .clk(Clck), .Q(Row7_bit3_q));  // open: reset, Qn, preset
  and and_31 (and_31_out, Read_Addr1_out, Row1_bit3_q);
  and and_32 (and_32_out, and_27_out, s_r_ff_2_q);
  S_R_Flip_Flop Row2_bit2 (.S(and_28_out), .R(and_29_out), .clk(Clck), .Q(Row2_bit2_q));  // open: reset, Qn, preset
  S_R_Flip_Flop Row3_bit2 (.S(and_30_out), .R(and_33_out), .clk(Clck), .Q(Row3_bit2_q));  // open: reset, Qn, preset
  and and_33 (and_33_out, and_9_out, not_23_out);
  not not_24 (not_24_out, Mode_Reg_qn);
  and and_34 (and_34_out, Addr6_and_Mode_out, s_r_ff_2_q);
  and and_35 (and_35_out, Addr6_and_Mode_out, not_25_out);
  not not_25 (not_25_out, s_r_ff_2_q);
  S_R_Flip_Flop Row0_bit1 (.S(and_22_out), .R(and_40_out), .clk(Clck), .Q(Row0_bit1_q));  // open: reset, Qn, preset
  not not_26 (not_26_out, s_r_ff_3_q);
  not not_27 (not_27_out, s_r_ff_2_q);
  and Read_Addr2_bit0 (Read_Addr2_bit0_out, Read_Addr2_out, Row2_bit3_q);
  and and_36 (and_36_out, Mode_and_Addr2_out, s_r_ff_3_q);
  not not_28 (not_28_out, s_r_ff_3_q);
  and and_37 (and_37_out, and_9_out, s_r_ff_3_q);
  and Read_Row4 (Read_Row4_out, Mode_Reg_q, Addr4_And_Gate_out);
  S_R_Flip_Flop Row4_bit2 (.S(and_46_out), .R(and_50_out), .clk(Clck), .Q(Row4_bit2_q));  // open: reset, Qn, preset
  and and_38 (and_38_out, Addr5_and_Mode_out, s_r_ff_2_q);
  S_R_Flip_Flop Row5_bit2 (.S(and_38_out), .R(and_51_out), .clk(Clck), .Q(Row5_bit2_q));  // open: reset, Qn, preset
  and Read_Row5 (Read_Row5_out, Addr5_And_Gate_out, not_24_out);
  S_R_Flip_Flop Row6_bit2 (.S(and_34_out), .R(and_35_out), .clk(Clck), .Q(Row6_bit2_q));  // open: reset, Qn, preset
  S_R_Flip_Flop Row7_bit2 (.S(and_39_out), .R(and_47_out), .clk(Clck), .Q(Row7_bit2_q));  // open: reset, Qn, preset
  and and_39 (and_39_out, Addr7_and_Mode_out, s_r_ff_2_q);
  not not_29 (not_29_out, s_r_ff_2_q);
  and and_40 (and_40_out, and_10_out, not_26_out);
  and and_41 (and_41_out, and_10_out, s_r_ff_4_q);
  and and_42 (and_42_out, and_27_out, not_27_out);
  S_R_Flip_Flop Row2_bit1 (.S(and_36_out), .R(and_43_out), .clk(Clck), .Q(Row2_bit1_q));  // open: reset, Qn, preset
  and and_43 (and_43_out, Mode_and_Addr2_out, not_28_out);
  S_R_Flip_Flop Row3_bit1 (.S(and_37_out), .R(and_44_out), .clk(Clck), .Q(Row3_bit1_q));  // open: reset, Qn, preset
  and and_44 (and_44_out, and_9_out, not_30_out);
  not not_30 (not_30_out, s_r_ff_3_q);
  and and_45 (and_45_out, Addr4_and_Mode_out, s_r_ff_1_q);
  and and_46 (and_46_out, Addr4_and_Mode_out, s_r_ff_2_q);
  not not_31 (not_31_out, s_r_ff_2_q);
  not not_32 (not_32_out, s_r_ff_3_q);
  and and_47 (and_47_out, Addr7_and_Mode_out, not_29_out);
  not not_33 (not_33_out, s_r_ff_4_q);
  S_R_Flip_Flop Row1_bit1 (.S(and_57_out), .R(and_58_out), .clk(Clck), .Q(Row1_bit1_q));  // open: reset, Qn, preset
  and and_48 (and_48_out, Mode_and_Addr2_out, s_r_ff_4_q);
  and and_49 (and_49_out, Read_Row4_out, Row4_bit3_q);
  and and_50 (and_50_out, Addr4_and_Mode_out, not_34_out);
  not not_34 (not_34_out, s_r_ff_2_q);
  and and_51 (and_51_out, Addr5_and_Mode_out, not_31_out);
  S_R_Flip_Flop Row5_bit1 (.S(and_61_out), .R(and_67_out), .clk(Clck), .Q(Row5_bit1_q));  // open: reset, Qn, preset
  and and_52 (and_52_out, Read_Row5_out, Row5_bit3_q);
  and and_53 (and_53_out, Addr6_and_Mode_out, s_r_ff_3_q);
  and and_54 (and_54_out, Addr6_and_Mode_out, not_32_out);
  and and_55 (and_55_out, Addr7_and_Mode_out, s_r_ff_3_q);
  not not_35 (not_35_out, s_r_ff_3_q);
  S_R_Flip_Flop Row0_bit0 (.S(and_41_out), .R(and_56_out), .clk(Clck), .Q(Row0_bit0_q));  // open: reset, Qn, preset
  and and_56 (and_56_out, and_10_out, not_33_out);
  and and_57 (and_57_out, Addr_and_Mode_out, s_r_ff_3_q);
  and and_58 (and_58_out, Addr_and_Mode_out, not_36_out);
  not not_36 (not_36_out, s_r_ff_3_q);
  not not_37 (not_37_out, s_r_ff_4_q);
  and and_59 (and_59_out, and_9_out, s_r_ff_4_q);
  not not_38 (not_38_out, s_r_ff_4_q);
  and and_60 (and_60_out, Addr4_and_Mode_out, s_r_ff_3_q);
  not not_39 (not_39_out, s_r_ff_3_q);
  S_R_Flip_Flop Row4_bit1 (.S(and_60_out), .R(and_66_out), .clk(Clck), .Q(Row4_bit1_q));  // open: reset, Qn, preset
  not not_40 (not_40_out, s_r_ff_3_q);
  and and_61 (and_61_out, Addr5_and_Mode_out, s_r_ff_3_q);
  S_R_Flip_Flop Row6_bit1 (.S(and_53_out), .R(and_54_out), .clk(Clck), .Q(Row6_bit1_q));  // open: reset, Qn, preset
  S_R_Flip_Flop Row7_bit1 (.S(and_55_out), .R(and_62_out), .clk(Clck), .Q(Row7_bit1_q));  // open: reset, Qn, preset
  and and_62 (and_62_out, Addr7_and_Mode_out, not_35_out);
  and Read_Addr0 (Read_Addr0_out, Addr0_And_Gate_out, Mode_Reg_q);
  and and_63 (and_63_out, Read_Addr0_out, Row0_bit0_q);
  S_R_Flip_Flop Row1_bit0 (.S(and_73_out), .R(and_74_out), .clk(Clck), .Q(Row1_bit0_q));  // open: reset, Qn, preset
  S_R_Flip_Flop Row2_bit0 (.S(and_48_out), .R(and_64_out), .clk(Clck), .Q(Row2_bit0_q));  // open: reset, Qn, preset
  and and_64 (and_64_out, Mode_and_Addr2_out, not_37_out);
  S_R_Flip_Flop Row3_bit0 (.S(and_59_out), .R(and_76_out), .clk(Clck), .Q(Row3_bit0_q));  // open: reset, Qn, preset
  and and_65 (and_65_out, Addr4_and_Mode_out, s_r_ff_4_q);
  and and_66 (and_66_out, Addr4_and_Mode_out, not_39_out);
  and and_67 (and_67_out, Addr5_and_Mode_out, not_40_out);
  and and_68 (and_68_out, Addr6_and_Mode_out, s_r_ff_4_q);
  and and_69 (and_69_out, Addr6_and_Mode_out, not_41_out);
  not not_41 (not_41_out, s_r_ff_4_q);
  not not_42 (not_42_out, s_r_ff_4_q);
  and and_70 (and_70_out, Read_Addr0_out, Row0_bit3_q);
  and and_71 (and_71_out, Read_Addr0_out, Row0_bit2_q);
  and and_72 (and_72_out, Read_Addr0_out, Row0_bit1_q);
  or or_1 (or_1_out, and_31_out, or_2_out);
  and and_73 (and_73_out, Addr_and_Mode_out, s_r_ff_4_q);
  and and_74 (and_74_out, Addr_and_Mode_out, not_43_out);
  not not_43 (not_43_out, s_r_ff_4_q);
  or or_2 (or_2_out, Read_Addr2_bit0_out, or_4_out);
  and and_75 (and_75_out, Row3_bit3_q, Read_Row3_out);
  and Read_Row3 (Read_Row3_out, Mode_Reg_q, Addr3_And_Gate_out);
  and and_76 (and_76_out, and_9_out, not_38_out);
  and and_77 (and_77_out, Addr4_and_Mode_out, not_44_out);
  not not_44 (not_44_out, s_r_ff_4_q);
  S_R_Flip_Flop Row4_bit0 (.S(and_65_out), .R(and_77_out), .clk(Clck), .Q(Row4_bit0_q));  // open: reset, Qn, preset
  and and_78 (and_78_out, Addr5_and_Mode_out, s_r_ff_4_q);
  not not_45 (not_45_out, s_r_ff_4_q);
  S_R_Flip_Flop Row5_bit0 (.S(and_78_out), .R(and_81_out), .clk(Clck), .Q(Row5_bit0_q));  // open: reset, Qn, preset
  S_R_Flip_Flop Row6_bit0 (.S(and_68_out), .R(and_69_out), .clk(Clck), .Q(Row6_bit0_q));  // open: reset, Qn, preset
  and and_79 (and_79_out, Addr7_and_Mode_out, s_r_ff_4_q);
  S_R_Flip_Flop Row7_bit0 (.S(and_79_out), .R(and_80_out), .clk(Clck), .Q(Row7_bit0_q));  // open: reset, Qn, preset
  and and_80 (and_80_out, Addr7_and_Mode_out, not_42_out);
  or or_3 (or_3_out, and_70_out, or_1_out);
  or or_4 (or_4_out, and_75_out, or_5_out);
  and and_81 (and_81_out, Addr5_and_Mode_out, not_45_out);
  and and_82 (and_82_out, Row6_bit3_q, Addr6_READ_out);
  and Addr6_READ (Addr6_READ_out, Mode_Reg_q, Addr6_And_Gate_out);
  and READ_Addr7 (READ_Addr7_out, Addr7_And_Gate_out, Mode_Reg_q);
  and and_83 (and_83_out, Read_Addr1_out, Row1_bit2_q);
  and and_84 (and_84_out, Row2_bit2_q, Read_Addr2_out);
  or or_5 (or_5_out, and_49_out, or_8_out);
  and READ_Addr7_BIT0 (READ_Addr7_BIT0_out, READ_Addr7_out, Row7_bit3_q);
  or or_6 (or_6_out, and_71_out, or_7_out);
  or or_7 (or_7_out, and_83_out, or_10_out);
  and and_85 (and_85_out, Row3_bit2_q, Read_Row3_out);
  or or_8 (or_8_out, and_52_out, or_9_out);
  and and_86 (and_86_out, Read_Row5_out, Row5_bit2_q);
  or or_9 (or_9_out, and_82_out, READ_Addr7_BIT0_out);
  and and_87 (and_87_out, Addr6_READ_out, Row6_bit2_q);
  and and_88 (and_88_out, READ_Addr7_out, Row7_bit2_q);
  or or_10 (or_10_out, and_84_out, or_14_out);
  and and_89 (and_89_out, Row4_bit2_q, Read_Row4_out);
  or or_11 (or_11_out, and_87_out, and_88_out);
  and and_90 (and_90_out, Read_Row3_out, Row3_bit1_q);
  or or_12 (or_12_out, and_89_out, or_13_out);
  or or_13 (or_13_out, and_86_out, or_11_out);
  and and_91 (and_91_out, Read_Addr1_out, Row1_bit1_q);
  and and_92 (and_92_out, Read_Addr2_out, Row2_bit1_q);
  or or_14 (or_14_out, and_85_out, or_12_out);
  and and_93 (and_93_out, Read_Row4_out, Row4_bit1_q);
  and and_94 (and_94_out, Row5_bit1_q, Read_Row5_out);
  and and_95 (and_95_out, Row6_bit1_q, Addr6_READ_out);
  and and_96 (and_96_out, Row7_bit1_q, READ_Addr7_out);
  or or_15 (or_15_out, and_91_out, or_16_out);
  or or_16 (or_16_out, and_92_out, or_19_out);
  or or_17 (or_17_out, and_94_out, or_18_out);
  or or_18 (or_18_out, and_95_out, and_96_out);
  and and_97 (and_97_out, READ_Addr7_out, Row7_bit0_q);
  and and_98 (and_98_out, Row1_bit0_q, Read_Addr1_out);
  and and_99 (and_99_out, Row2_bit0_q, Read_Addr2_out);
  or or_19 (or_19_out, and_90_out, or_20_out);
  and and_100 (and_100_out, Read_Row3_out, Row3_bit0_q);
  or or_20 (or_20_out, and_93_out, or_17_out);
  and and_101 (and_101_out, Read_Row4_out, Row4_bit0_q);
  and and_102 (and_102_out, Row5_bit0_q, Read_Row5_out);
  and and_103 (and_103_out, Row6_bit0_q, Addr6_READ_out);
  or or_21 (or_21_out, and_72_out, or_15_out);
  or or_22 (or_22_out, and_99_out, or_26_out);
  or or_23 (or_23_out, and_102_out, or_24_out);
  or or_24 (or_24_out, and_103_out, and_97_out);
  or or_25 (or_25_out, and_98_out, or_22_out);
  or or_26 (or_26_out, and_100_out, or_27_out);
  or or_27 (or_27_out, and_101_out, or_23_out);
  or or_28 (or_28_out, and_63_out, or_25_out);
  D_Flip_Flop d_ff_1 (.D(or_3_out), .clk(Clck), .Q(Data_Output_Bit3));  // open: Qn, preset, reset
  D_Flip_Flop d_ff_2 (.D(or_6_out), .clk(Clck), .Q(Data_Output_Bit2));  // open: Qn, preset, reset
  D_Flip_Flop d_ff_3 (.D(or_21_out), .clk(Clck), .Q(Data_Output_Bit1));  // open: Qn, preset, reset
  D_Flip_Flop d_ff_4 (.D(or_28_out), .clk(Clck), .Q(Data_Output_Bit0));  // open: Qn, preset, reset
endmodule

module ALU (
  input  clck,
  input  L_Input3,
  input  L_Input2,
  input  L_Input1,
  input  L_Input0,
  input  R_Input3,
  input  R_Input2,
  input  R_Input1,
  input  R_Input0,
  input  Add_Sub,
  output Negative_Status_Output1_Bit0,
  output Zero_Status_Output2_Bit1,
  output Magnitude_Overflow_Status_Output3_Bit2,
  output A_Output3,
  output A_Output2,
  output A_Output1,
  output A_Output0
);

  wire and_1_out, and_2_out, and_3_out, and_4_out, Bit3_In_And_Out_Carries2_out, Bit3_In_And_Out_Carries_out,
       Carry1_out, Carry2_out, Carry3_out, L1R1_Carry_out, L2_add_R2_out, L2_AND_Carry_out, L2_AND_R2_out,
       L2_R2_Carry_out, L3_AND_Carry_out, L3_AND_R3_out, L3_R3_Carry_out, L3_R3_out, L4_AND_Carry_out,
       L4_AND_R4_out, L4_R4_Carry_out, L4_R4_out, Magnitude_Overflow_out, Not2sCompl1_out, Not2sCompl2_out,
       Not2sCompl3_out, Not2sCompl4_out, not_1_out, not_2_out, not_3_out, not_4_out, not_5_out, not_6_out,
       not_7_out, not_8_out, not_9_out, not_10_out, not_11_out, or_1_out, or_2_out, or_3_out, or_4_out,
       or_5_out, or_6_out, R1_out, R2_AND_Carry_out, R2_out, R3_AND_Carry_out, R3_out, R4_AND_Carry_out,
       R4_out, Twos_Compl1_out, Twos_Compl2_out, Twos_Compl3_out, Twos_Compl4_out;

  not not_1 (not_1_out, R_Input0);
  not not_2 (not_2_out, R_Input1);
  not not_3 (not_3_out, R_Input2);
  not not_4 (not_4_out, R_Input3);
  and Carry1 (Carry1_out, not_1_out, Add_Sub);
  and Carry3 (Carry3_out, Carry2_out, not_3_out);
  and Carry2 (Carry2_out, not_2_out, Carry1_out);
  xor Twos_Compl1 (Twos_Compl1_out, not_1_out, Add_Sub);
  not not_5 (not_5_out, Add_Sub);
  and and_1 (and_1_out, Twos_Compl1_out, Add_Sub);
  not not_6 (not_6_out, Add_Sub);
  xor Twos_Compl2 (Twos_Compl2_out, not_2_out, Carry1_out);
  not not_7 (not_7_out, Add_Sub);
  xor Twos_Compl3 (Twos_Compl3_out, Carry2_out, not_3_out);
  xor Twos_Compl4 (Twos_Compl4_out, not_4_out, Carry3_out);
  not not_8 (not_8_out, Add_Sub);
  and Not2sCompl1 (Not2sCompl1_out, not_5_out, R_Input0);
  and Not2sCompl2 (Not2sCompl2_out, not_6_out, R_Input1);
  and and_2 (and_2_out, Twos_Compl2_out, Add_Sub);
  and Not2sCompl3 (Not2sCompl3_out, not_7_out, R_Input2);
  and and_3 (and_3_out, Twos_Compl3_out, Add_Sub);
  and and_4 (and_4_out, Twos_Compl4_out, Add_Sub);
  and Not2sCompl4 (Not2sCompl4_out, R_Input3, not_8_out);
  or R1 (R1_out, and_1_out, Not2sCompl1_out);
  or R2 (R2_out, and_2_out, Not2sCompl2_out);
  or R3 (R3_out, and_3_out, Not2sCompl3_out);
  or R4 (R4_out, and_4_out, Not2sCompl4_out);
  and L1R1_Carry (L1R1_Carry_out, L_Input0, R1_out);
  xor L2_add_R2 (L2_add_R2_out, L_Input1, R2_out);
  and R2_AND_Carry (R2_AND_Carry_out, R2_out, L1R1_Carry_out);
  xor A0 (A_Output0, L_Input0, R1_out);
  xor A1 (A_Output1, L1R1_Carry_out, L2_add_R2_out);
  and L2_AND_R2 (L2_AND_R2_out, L_Input1, R2_out);
  and L2_AND_Carry (L2_AND_Carry_out, L1R1_Carry_out, L_Input1);
  xor L3_R3 (L3_R3_out, R3_out, L_Input2);
  and L3_AND_R3 (L3_AND_R3_out, L_Input2, R3_out);
  and L3_AND_Carry (L3_AND_Carry_out, L2_R2_Carry_out, L_Input2);
  xor L4_R4 (L4_R4_out, L_Input3, R4_out);
  and L4_AND_R4 (L4_AND_R4_out, L_Input3, R4_out);
  or or_1 (or_1_out, L2_AND_R2_out, R2_AND_Carry_out);
  and L4_AND_Carry (L4_AND_Carry_out, L_Input3, L3_R3_Carry_out);
  or L2_R2_Carry (L2_R2_Carry_out, or_1_out, L2_AND_Carry_out);
  xor A2 (A_Output2, L3_R3_out, L2_R2_Carry_out);
  or or_2 (or_2_out, L3_AND_R3_out, L3_AND_Carry_out);
  and R3_AND_Carry (R3_AND_Carry_out, R3_out, L2_R2_Carry_out);
  xor A3 (A_Output3, L4_R4_out, L3_R3_Carry_out);
  or or_3 (or_3_out, L4_AND_R4_out, L4_AND_Carry_out);
  and R4_AND_Carry (R4_AND_Carry_out, L3_R3_Carry_out, R4_out);
  or L3_R3_Carry (L3_R3_Carry_out, or_2_out, R3_AND_Carry_out);
  or L4_R4_Carry (L4_R4_Carry_out, or_3_out, R4_AND_Carry_out);
  or or_4 (or_4_out, A_Output1, or_5_out);
  or or_5 (or_5_out, A_Output2, A_Output3);
  or or_6 (or_6_out, A_Output0, or_4_out);
  not not_9 (not_9_out, or_6_out);
  not not_10 (not_10_out, L3_R3_Carry_out);
  D_Flip_Flop d_ff_1 (.D(A_Output3), .clk(clck), .Q(Negative_Status_Output1_Bit0));  // open: Qn, preset, reset
  D_Flip_Flop d_ff_2 (.D(not_9_out), .clk(clck), .Q(Zero_Status_Output2_Bit1));  // open: Qn, preset, reset
  D_Flip_Flop d_ff_3 (
    .D(Magnitude_Overflow_out), .clk(clck), .Q(Magnitude_Overflow_Status_Output3_Bit2));  // open: Qn, preset, reset
  and Bit3_In_And_Out_Carries (Bit3_In_And_Out_Carries_out, not_10_out, L4_R4_Carry_out);
  not not_11 (not_11_out, L4_R4_Carry_out);
  and Bit3_In_And_Out_Carries2 (Bit3_In_And_Out_Carries2_out, L3_R3_Carry_out, not_11_out);
  or Magnitude_Overflow (Magnitude_Overflow_out, Bit3_In_And_Out_Carries_out, Bit3_In_And_Out_Carries2_out);
endmodule

module CU (
  input  clck,
  input  IR3,
  input  IR2,
  input  IR1,
  input  IR0,
  output Mode,
  output ld_R1_0,
  output ld_R0_1,
  output ld_R1_1,
  output sv_R0_0,
  output sv_R0_1,
  output sv_R1_0,
  output sv_R1_1,
  output add_R0_R0,
  output add_R0_R1,
  output add_R1_R0,
  output add_R1_R1,
  output sub_R0_R0,
  output sub_R0_R1,
  output sub_R1_R0,
  output Halt,
  output Jump
);

  wire add, and_1_out, and_4_out, and_7_out, and_10_out, and_12_out, and_13_out, and_15_out, and_17_out,
       and_19_out, and_21_out, and_24_out, and_26_out, and_28_out, and_29_out, and_30_out, and_31_out,
       and_33_out, and_34_out, ld_gate, not_1_out, not_2_out, not_3_out, not_4_out, not_5_out, not_6_out,
       not_7_out, not_8_out, not_9_out, not_10_out, not_11_out, not_12_out, not_13_out, not_14_out,
       not_15_out, not_16_out, not_17_out, not_18_out, not_19_out, not_20_out, not_21_out, not_22_out,
       or_1_out, save, sub;

  and and_1 (and_1_out, IR1, IR0);
  not not_1 (not_1_out, IR1);
  not not_2 (not_2_out, IR3);
  and loadGate (ld_gate, not_2_out, not_7_out);
  and and_2 (add_R1_R1, add, and_28_out);
  and and_3 (sub, IR3, IR2);
  not not_3 (not_3_out, IR1);
  and and_4 (and_4_out, not_3_out, not_14_out);
  and and_5 (sub_R0_R0, sub, and_4_out);
  not not_4 (not_4_out, IR1);
  and and_6 (sub_R0_R1, sub, and_29_out);
  not not_5 (not_5_out, IR1);
  and and_7 (and_7_out, not_5_out, IR0);
  and and_8 (sub_R1_R0, sub, and_7_out);
  and and_9 (Halt, and_1_out, and_30_out);
  not not_6 (not_6_out, IR0);
  and and_10 (and_10_out, not_1_out, not_6_out);
  and and_11 (Jump, and_10_out, and_31_out);
  not not_7 (not_7_out, IR2);
  and and_12 (and_12_out, ld_gate, IR1);
  and load_R1_addrs0 (ld_R1_0, and_12_out, not_19_out);
  and and_13 (and_13_out, ld_gate, not_17_out);
  and and_14 (ld_R0_1, and_13_out, IR0);
  and and_15 (and_15_out, ld_gate, IR1);
  and and_16 (ld_R1_1, and_15_out, IR0);
  not not_8 (not_8_out, IR3);
  and save_gate (save, not_8_out, IR2);
  not not_9 (not_9_out, IR1);
  and and_17 (and_17_out, not_9_out, IR0);
  and and_18 (sv_R0_1, save, and_17_out);
  and and_19 (and_19_out, IR1, not_18_out);
  and and_20 (sv_R1_0, save, and_19_out);
  and and_21 (and_21_out, IR1, IR0);
  and and_22 (sv_R1_1, save, and_21_out);
  not not_10 (not_10_out, IR2);
  and and_23 (add, IR3, not_10_out);
  not not_11 (not_11_out, IR1);
  not not_12 (not_12_out, IR0);
  and and_24 (and_24_out, not_11_out, not_12_out);
  and and_25 (add_R0_R0, add, and_24_out);
  not not_13 (not_13_out, IR1);
  and and_26 (and_26_out, not_13_out, IR0);
  and and_27 (add_R0_R1, add, and_26_out);
  and and_28 (and_28_out, IR1, IR0);
  not not_14 (not_14_out, IR0);
  and and_29 (and_29_out, not_4_out, IR0);
  and and_30 (and_30_out, IR3, IR2);
  not not_15 (not_15_out, IR3);
  not not_16 (not_16_out, IR2);
  and and_31 (and_31_out, not_15_out, not_16_out);
  not not_17 (not_17_out, IR1);
  not not_18 (not_18_out, IR0);
  not not_19 (not_19_out, IR0);
  not not_20 (not_20_out, IR1);
  and and_32 (sv_R0_0, save, and_33_out);
  not not_21 (not_21_out, IR0);
  and and_33 (and_33_out, not_20_out, not_21_out);
  not not_22 (not_22_out, IR0);
  and and_34 (and_34_out, IR1, not_22_out);
  and and_35 (add_R1_R0, add, and_34_out);
  or or_1 (or_1_out, ld_R1_0, ld_R0_1);
  or or_2 (Mode, or_1_out, ld_R1_1);

  // Other names for the same wires on the sheet: load_R0_1 = ld_R0_1; load_R1_0 = ld_R1_0; load_R1_1 = ld_R1_1;
  //   save_R0_0 = sv_R0_0; save_R0_1 = sv_R0_1; save_R1_0 = sv_R1_0; save_R1_1 = sv_R1_1

  // Notes on the sheet:
  //   Instructions:
  //   Halt
  //   Load (00xx)
  //   0010
  //   0001
  //   0011
  //   Save (01xx)
  //   0100
  //   0110
  //   0111
  //   Arithmetic Instructions
  //   Add (10xx)
  //   1000
  //   1011
  //   Sub (11xx)
  //   1100
  //   1101
  //   1110
  //   Jump
  //   0101
  //   1001 
  //   Opcode
  //   1010
  //   Load Instructions for mode
  //   Output Pins:
  //   Load Instruction:
  //   Save Instruction:
  //   Add
  //   Sub
  //   Halt
  //   Jump
endmodule

module Data_RAM (
  input  Clck,
  input  Mode_Input_Pin,
  input  Address_Bit0,
  input  Address_Bit1,
  input  Address_Bit2,
  input  Data_Input_Bit3,
  input  Data_Input_Bit2,
  input  Data_Input_Bit1,
  input  Data_Input_Bit0,
  output Output_Bit3,
  output Output_Bit2,
  output Output_Bit1,
  output Output_Bit0
);

  wire Addr0_And_Gate_out, Addr1_And_Gate_out, Addr2_And_Gate_out, Addr3_And_Gate_out, Addr4_And_Gate_out,
       Addr4_and_Mode_out, Addr5_And_Gate_out, Addr5_and_Mode_out, Addr6_And_Gate_out, Addr6_and_Mode_out,
       Addr6_READ_out, Addr7_And_Gate_out, Addr7_and_Mode_out, Addr_and_Mode_out, and_1_out, and_2_out,
       and_3_out, and_4_out, and_5_out, and_6_out, and_7_out, and_8_out, and_9_out, and_10_out, and_11_out,
       and_12_out, and_13_out, and_14_out, and_15_out, and_16_out, and_17_out, and_18_out, and_19_out,
       and_20_out, and_21_out, and_22_out, and_23_out, and_24_out, and_25_out, and_26_out, and_27_out,
       and_28_out, and_29_out, and_30_out, and_31_out, and_32_out, and_33_out, and_34_out, and_35_out,
       and_36_out, and_37_out, and_38_out, and_39_out, and_40_out, and_41_out, and_42_out, and_43_out,
       and_44_out, and_45_out, and_46_out, and_47_out, and_48_out, and_49_out, and_50_out, and_51_out,
       and_52_out, and_53_out, and_54_out, and_55_out, and_56_out, and_57_out, and_58_out, and_59_out,
       and_60_out, and_61_out, and_62_out, and_63_out, and_64_out, and_65_out, and_66_out, and_67_out,
       and_68_out, and_69_out, and_70_out, and_71_out, and_72_out, and_73_out, and_74_out, and_75_out,
       and_76_out, and_77_out, and_78_out, and_79_out, and_80_out, and_81_out, and_82_out, and_83_out,
       and_84_out, and_85_out, and_86_out, and_87_out, and_88_out, and_89_out, and_90_out, and_91_out,
       and_92_out, and_93_out, and_94_out, and_95_out, and_96_out, and_97_out, and_98_out, and_99_out,
       and_100_out, and_101_out, and_102_out, and_103_out, Data_And_Gate3_out, Data_And_Gate_out,
       Mode_and_Addr2_out, Mode_Reg_q, Mode_Reg_qn, not_1_out, not_2_out, not_3_out, not_4_out, not_5_out,
       not_6_out, not_7_out, not_8_out, not_9_out, not_10_out, not_11_out, not_12_out, not_13_out,
       not_14_out, not_15_out, not_16_out, not_17_out, not_18_out, not_19_out, not_20_out, not_21_out,
       not_22_out, not_23_out, not_24_out, not_25_out, not_26_out, not_27_out, not_28_out, not_29_out,
       not_30_out, not_31_out, not_32_out, not_33_out, not_34_out, not_35_out, not_36_out, not_37_out,
       not_38_out, not_39_out, not_40_out, not_41_out, not_42_out, not_43_out, not_44_out, not_45_out,
       or_1_out, or_2_out, or_3_out, or_4_out, or_5_out, or_6_out, or_7_out, or_8_out, or_9_out, or_10_out,
       or_11_out, or_12_out, or_13_out, or_14_out, or_15_out, or_16_out, or_17_out, or_18_out, or_19_out,
       or_20_out, or_21_out, or_22_out, or_23_out, or_24_out, or_25_out, or_26_out, or_27_out, or_28_out,
       Read_Addr0_out, Read_Addr1_out, Read_Addr2_bit0_out, Read_Addr2_out, READ_Addr7_BIT0_out,
       READ_Addr7_out, Read_Row3_out, Read_Row4_out, Read_Row5_out, Row0_bit0_q, Row0_bit1_q, Row0_bit2_q,
       Row0_bit3_q, Row1_bit0_q, Row1_bit1_q, Row1_bit2_q, Row1_bit3_q, Row2_bit0_q, Row2_bit1_q,
       Row2_bit2_q, Row2_bit3_q, Row3_bit0_q, Row3_bit1_q, Row3_bit2_q, Row3_bit3_q, Row4_bit0_q,
       Row4_bit1_q, Row4_bit2_q, Row4_bit3_q, Row5_bit0_q, Row5_bit1_q, Row5_bit2_q, Row5_bit3_q,
       Row6_bit0_q, Row6_bit1_q, Row6_bit2_q, Row6_bit3_q, Row7_bit0_q, Row7_bit1_q, Row7_bit2_q,
       Row7_bit3_q, s_r_ff_1_q, s_r_ff_2_q, s_r_ff_3_q, s_r_ff_4_q, s_r_ff_5_q, s_r_ff_5_qn, s_r_ff_6_q,
       s_r_ff_6_qn, s_r_ff_7_q, s_r_ff_7_qn;

  not not_1 (not_1_out, Data_Input_Bit3);
  not not_2 (not_2_out, Data_Input_Bit2);
  not not_3 (not_3_out, Data_Input_Bit1);
  not not_4 (not_4_out, Data_Input_Bit0);
  D_Flip_Flop Mode_Reg (.D(Mode_Input_Pin), .clk(Clck), .Q(Mode_Reg_q), .Qn(Mode_Reg_qn));  // open: preset, reset
  S_R_Flip_Flop s_r_ff_1 (.S(Data_Input_Bit3), .R(not_1_out), .clk(Clck), .Q(s_r_ff_1_q));  // open: reset, Qn, preset
  S_R_Flip_Flop s_r_ff_2 (.S(Data_Input_Bit2), .R(not_2_out), .clk(Clck), .Q(s_r_ff_2_q));  // open: reset, Qn, preset
  S_R_Flip_Flop s_r_ff_3 (.S(Data_Input_Bit1), .R(not_3_out), .clk(Clck), .Q(s_r_ff_3_q));  // open: reset, Qn, preset
  S_R_Flip_Flop s_r_ff_4 (.S(Data_Input_Bit0), .R(not_4_out), .clk(Clck), .Q(s_r_ff_4_q));  // open: reset, Qn, preset
  not not_5 (not_5_out, Address_Bit0);
  not not_6 (not_6_out, Address_Bit1);
  not not_7 (not_7_out, Address_Bit2);
  S_R_Flip_Flop s_r_ff_5 (
    .S(Address_Bit0), .R(not_5_out), .clk(Clck), .Q(s_r_ff_5_q), .Qn(s_r_ff_5_qn));  // open: reset, preset
  S_R_Flip_Flop s_r_ff_6 (
    .S(Address_Bit1), .R(not_6_out), .clk(Clck), .Q(s_r_ff_6_q), .Qn(s_r_ff_6_qn));  // open: reset, preset
  S_R_Flip_Flop s_r_ff_7 (
    .S(Address_Bit2), .R(not_7_out), .clk(Clck), .Q(s_r_ff_7_q), .Qn(s_r_ff_7_qn));  // open: reset, preset
  and and_1 (and_1_out, s_r_ff_5_qn, s_r_ff_6_q);
  not not_8 (not_8_out, s_r_ff_5_qn);
  and and_2 (and_2_out, s_r_ff_5_qn, s_r_ff_6_q);
  and and_3 (and_3_out, s_r_ff_5_qn, s_r_ff_6_qn);
  and Addr6_And_Gate (Addr6_And_Gate_out, and_1_out, s_r_ff_7_q);
  and and_4 (and_4_out, s_r_ff_6_q, not_8_out);
  not not_9 (not_9_out, s_r_ff_5_q);
  not not_10 (not_10_out, s_r_ff_6_q);
  and Addr2_And_Gate (Addr2_And_Gate_out, and_2_out, s_r_ff_7_qn);
  and and_5 (and_5_out, s_r_ff_5_q, s_r_ff_6_qn);
  and Addr7_And_Gate (Addr7_And_Gate_out, and_4_out, s_r_ff_7_q);
  and and_6 (and_6_out, not_9_out, not_10_out);
  not not_11 (not_11_out, s_r_ff_7_q);
  and and_7 (and_7_out, s_r_ff_5_q, not_10_out);
  and and_8 (and_8_out, s_r_ff_5_q, s_r_ff_6_q);
  and Addr4_And_Gate (Addr4_And_Gate_out, and_3_out, s_r_ff_7_q);
  and Addr5_And_Gate (Addr5_And_Gate_out, and_5_out, s_r_ff_7_q);
  and Addr6_and_Mode (Addr6_and_Mode_out, Addr6_And_Gate_out, Mode_Reg_qn);
  and Mode_and_Addr2 (Mode_and_Addr2_out, Addr2_And_Gate_out, Mode_Reg_qn);
  and Addr3_And_Gate (Addr3_And_Gate_out, and_8_out, s_r_ff_7_qn);
  and and_9 (and_9_out, Addr3_And_Gate_out, Mode_Reg_qn);
  and Addr4_and_Mode (Addr4_and_Mode_out, Addr4_And_Gate_out, Mode_Reg_qn);
  and Addr5_and_Mode (Addr5_and_Mode_out, Addr5_And_Gate_out, Mode_Reg_qn);
  and Addr7_and_Mode (Addr7_and_Mode_out, Addr7_And_Gate_out, Mode_Reg_qn);
  and Addr0_And_Gate (Addr0_And_Gate_out, and_6_out, not_11_out);
  and Addr1_And_Gate (Addr1_And_Gate_out, not_11_out, and_7_out);
  and and_10 (and_10_out, Mode_Reg_qn, Addr0_And_Gate_out);
  and Addr_and_Mode (Addr_and_Mode_out, Addr1_And_Gate_out, Mode_Reg_qn);
  and Data_And_Gate (Data_And_Gate_out, Mode_and_Addr2_out, s_r_ff_1_q);
  not not_12 (not_12_out, s_r_ff_1_q);
  not not_13 (not_13_out, s_r_ff_1_q);
  not not_14 (not_14_out, s_r_ff_1_q);
  not not_15 (not_15_out, s_r_ff_1_q);
  not not_16 (not_16_out, s_r_ff_1_q);
  S_R_Flip_Flop Row0_bit3 (.S(and_11_out), .R(and_20_out), .clk(Clck), .Q(Row0_bit3_q));  // open: reset, Qn, preset
  and and_11 (and_11_out, and_10_out, s_r_ff_1_q);
  not not_17 (not_17_out, s_r_ff_1_q);
  S_R_Flip_Flop Row1_bit3 (.S(and_12_out), .R(and_23_out), .clk(Clck), .Q(Row1_bit3_q));  // open: reset, Qn, preset
  and and_12 (and_12_out, Addr_and_Mode_out, s_r_ff_1_q);
  not not_18 (not_18_out, s_r_ff_1_q);
  and and_13 (and_13_out, Mode_and_Addr2_out, not_12_out);
  not not_19 (not_19_out, s_r_ff_2_q);
  and Data_And_Gate3 (Data_And_Gate3_out, and_9_out, s_r_ff_1_q);
  not not_20 (not_20_out, s_r_ff_1_q);
  and and_14 (and_14_out, Addr4_and_Mode_out, not_13_out);
  and and_15 (and_15_out, Addr5_and_Mode_out, s_r_ff_1_q);
  and and_16 (and_16_out, Addr5_and_Mode_out, not_14_out);
  and and_17 (and_17_out, Addr6_and_Mode_out, s_r_ff_1_q);
  and and_18 (and_18_out, s_r_ff_1_q, Addr7_and_Mode_out);
  and and_19 (and_19_out, Addr7_and_Mode_out, not_16_out);
  and and_20 (and_20_out, and_10_out, not_17_out);
  and and_21 (and_21_out, and_10_out, s_r_ff_2_q);
  not not_21 (not_21_out, s_r_ff_2_q);
  and and_22 (and_22_out, and_10_out, s_r_ff_3_q);
  and and_23 (and_23_out, Addr_and_Mode_out, not_18_out);
  not not_22 (not_22_out, Mode_Reg_qn);
  S_R_Flip_Flop Row2_bit3 (
    .S(Data_And_Gate_out), .R(and_13_out), .clk(Clck), .Q(Row2_bit3_q));  // open: reset, Qn, preset
  S_R_Flip_Flop Row3_bit3 (
    .S(Data_And_Gate3_out), .R(and_24_out), .clk(Clck), .Q(Row3_bit3_q));  // open: reset, Qn, preset
  and and_24 (and_24_out, and_9_out, not_20_out);
  and and_25 (and_25_out, Addr6_and_Mode_out, not_15_out);
  S_R_Flip_Flop Row0_bit2 (.S(and_21_out), .R(and_26_out), .clk(Clck), .Q(Row0_bit2_q));  // open: reset, Qn, preset
  and and_26 (and_26_out, and_10_out, not_21_out);
  and Read_Addr1 (Read_Addr1_out, Addr1_And_Gate_out, Mode_Reg_q);
  S_R_Flip_Flop Row1_bit2 (.S(and_32_out), .R(and_42_out), .clk(Clck), .Q(Row1_bit2_q));  // open: reset, Qn, preset
  and and_27 (and_27_out, Addr1_And_Gate_out, Mode_Reg_qn);
  and Read_Addr2 (Read_Addr2_out, Addr2_And_Gate_out, not_22_out);
  and and_28 (and_28_out, Mode_and_Addr2_out, s_r_ff_2_q);
  and and_29 (and_29_out, Mode_and_Addr2_out, not_19_out);
  and and_30 (and_30_out, and_9_out, s_r_ff_2_q);
  not not_23 (not_23_out, s_r_ff_2_q);
  S_R_Flip_Flop Row4_bit3 (.S(and_45_out), .R(and_14_out), .clk(Clck), .Q(Row4_bit3_q));  // open: reset, Qn, preset
  S_R_Flip_Flop Row5_bit3 (.S(and_15_out), .R(and_16_out), .clk(Clck), .Q(Row5_bit3_q));  // open: reset, Qn, preset
  S_R_Flip_Flop Row6_bit3 (.S(and_17_out), .R(and_25_out), .clk(Clck), .Q(Row6_bit3_q));  // open: reset, Qn, preset
  S_R_Flip_Flop Row7_bit3 (.S(and_18_out), .R(and_19_out), .clk(Clck), .Q(Row7_bit3_q));  // open: reset, Qn, preset
  and and_31 (and_31_out, Read_Addr1_out, Row1_bit3_q);
  and and_32 (and_32_out, and_27_out, s_r_ff_2_q);
  S_R_Flip_Flop Row2_bit2 (.S(and_28_out), .R(and_29_out), .clk(Clck), .Q(Row2_bit2_q));  // open: reset, Qn, preset
  S_R_Flip_Flop Row3_bit2 (.S(and_30_out), .R(and_33_out), .clk(Clck), .Q(Row3_bit2_q));  // open: reset, Qn, preset
  and and_33 (and_33_out, and_9_out, not_23_out);
  not not_24 (not_24_out, Mode_Reg_qn);
  and and_34 (and_34_out, Addr6_and_Mode_out, s_r_ff_2_q);
  and and_35 (and_35_out, Addr6_and_Mode_out, not_25_out);
  not not_25 (not_25_out, s_r_ff_2_q);
  S_R_Flip_Flop Row0_bit1 (.S(and_22_out), .R(and_40_out), .clk(Clck), .Q(Row0_bit1_q));  // open: reset, Qn, preset
  not not_26 (not_26_out, s_r_ff_3_q);
  not not_27 (not_27_out, s_r_ff_2_q);
  and Read_Addr2_bit0 (Read_Addr2_bit0_out, Read_Addr2_out, Row2_bit3_q);
  and and_36 (and_36_out, Mode_and_Addr2_out, s_r_ff_3_q);
  not not_28 (not_28_out, s_r_ff_3_q);
  and and_37 (and_37_out, and_9_out, s_r_ff_3_q);
  and Read_Row4 (Read_Row4_out, Mode_Reg_q, Addr4_And_Gate_out);
  S_R_Flip_Flop Row4_bit2 (.S(and_46_out), .R(and_50_out), .clk(Clck), .Q(Row4_bit2_q));  // open: reset, Qn, preset
  and and_38 (and_38_out, Addr5_and_Mode_out, s_r_ff_2_q);
  S_R_Flip_Flop Row5_bit2 (.S(and_38_out), .R(and_51_out), .clk(Clck), .Q(Row5_bit2_q));  // open: reset, Qn, preset
  and Read_Row5 (Read_Row5_out, Addr5_And_Gate_out, not_24_out);
  S_R_Flip_Flop Row6_bit2 (.S(and_34_out), .R(and_35_out), .clk(Clck), .Q(Row6_bit2_q));  // open: reset, Qn, preset
  S_R_Flip_Flop Row7_bit2 (.S(and_39_out), .R(and_47_out), .clk(Clck), .Q(Row7_bit2_q));  // open: reset, Qn, preset
  and and_39 (and_39_out, Addr7_and_Mode_out, s_r_ff_2_q);
  not not_29 (not_29_out, s_r_ff_2_q);
  and and_40 (and_40_out, and_10_out, not_26_out);
  and and_41 (and_41_out, and_10_out, s_r_ff_4_q);
  and and_42 (and_42_out, and_27_out, not_27_out);
  S_R_Flip_Flop Row2_bit1 (.S(and_36_out), .R(and_43_out), .clk(Clck), .Q(Row2_bit1_q));  // open: reset, Qn, preset
  and and_43 (and_43_out, Mode_and_Addr2_out, not_28_out);
  S_R_Flip_Flop Row3_bit1 (.S(and_37_out), .R(and_44_out), .clk(Clck), .Q(Row3_bit1_q));  // open: reset, Qn, preset
  and and_44 (and_44_out, and_9_out, not_30_out);
  not not_30 (not_30_out, s_r_ff_3_q);
  and and_45 (and_45_out, Addr4_and_Mode_out, s_r_ff_1_q);
  and and_46 (and_46_out, Addr4_and_Mode_out, s_r_ff_2_q);
  not not_31 (not_31_out, s_r_ff_2_q);
  not not_32 (not_32_out, s_r_ff_3_q);
  and and_47 (and_47_out, Addr7_and_Mode_out, not_29_out);
  not not_33 (not_33_out, s_r_ff_4_q);
  S_R_Flip_Flop Row1_bit1 (.S(and_57_out), .R(and_58_out), .clk(Clck), .Q(Row1_bit1_q));  // open: reset, Qn, preset
  and and_48 (and_48_out, Mode_and_Addr2_out, s_r_ff_4_q);
  and and_49 (and_49_out, Read_Row4_out, Row4_bit3_q);
  and and_50 (and_50_out, Addr4_and_Mode_out, not_34_out);
  not not_34 (not_34_out, s_r_ff_2_q);
  and and_51 (and_51_out, Addr5_and_Mode_out, not_31_out);
  S_R_Flip_Flop Row5_bit1 (.S(and_61_out), .R(and_67_out), .clk(Clck), .Q(Row5_bit1_q));  // open: reset, Qn, preset
  and and_52 (and_52_out, Read_Row5_out, Row5_bit3_q);
  and and_53 (and_53_out, Addr6_and_Mode_out, s_r_ff_3_q);
  and and_54 (and_54_out, Addr6_and_Mode_out, not_32_out);
  and and_55 (and_55_out, Addr7_and_Mode_out, s_r_ff_3_q);
  not not_35 (not_35_out, s_r_ff_3_q);
  S_R_Flip_Flop Row0_bit0 (.S(and_41_out), .R(and_56_out), .clk(Clck), .Q(Row0_bit0_q));  // open: reset, Qn, preset
  and and_56 (and_56_out, and_10_out, not_33_out);
  and and_57 (and_57_out, Addr_and_Mode_out, s_r_ff_3_q);
  and and_58 (and_58_out, Addr_and_Mode_out, not_36_out);
  not not_36 (not_36_out, s_r_ff_3_q);
  not not_37 (not_37_out, s_r_ff_4_q);
  and and_59 (and_59_out, and_9_out, s_r_ff_4_q);
  not not_38 (not_38_out, s_r_ff_4_q);
  and and_60 (and_60_out, Addr4_and_Mode_out, s_r_ff_3_q);
  not not_39 (not_39_out, s_r_ff_3_q);
  S_R_Flip_Flop Row4_bit1 (.S(and_60_out), .R(and_66_out), .clk(Clck), .Q(Row4_bit1_q));  // open: reset, Qn, preset
  not not_40 (not_40_out, s_r_ff_3_q);
  and and_61 (and_61_out, Addr5_and_Mode_out, s_r_ff_3_q);
  S_R_Flip_Flop Row6_bit1 (.S(and_53_out), .R(and_54_out), .clk(Clck), .Q(Row6_bit1_q));  // open: reset, Qn, preset
  S_R_Flip_Flop Row7_bit1 (.S(and_55_out), .R(and_62_out), .clk(Clck), .Q(Row7_bit1_q));  // open: reset, Qn, preset
  and and_62 (and_62_out, Addr7_and_Mode_out, not_35_out);
  and Read_Addr0 (Read_Addr0_out, Addr0_And_Gate_out, Mode_Reg_q);
  and and_63 (and_63_out, Read_Addr0_out, Row0_bit0_q);
  S_R_Flip_Flop Row1_bit0 (.S(and_73_out), .R(and_74_out), .clk(Clck), .Q(Row1_bit0_q));  // open: reset, Qn, preset
  S_R_Flip_Flop Row2_bit0 (.S(and_48_out), .R(and_64_out), .clk(Clck), .Q(Row2_bit0_q));  // open: reset, Qn, preset
  and and_64 (and_64_out, Mode_and_Addr2_out, not_37_out);
  S_R_Flip_Flop Row3_bit0 (.S(and_59_out), .R(and_76_out), .clk(Clck), .Q(Row3_bit0_q));  // open: reset, Qn, preset
  and and_65 (and_65_out, Addr4_and_Mode_out, s_r_ff_4_q);
  and and_66 (and_66_out, Addr4_and_Mode_out, not_39_out);
  and and_67 (and_67_out, Addr5_and_Mode_out, not_40_out);
  and and_68 (and_68_out, Addr6_and_Mode_out, s_r_ff_4_q);
  and and_69 (and_69_out, Addr6_and_Mode_out, not_41_out);
  not not_41 (not_41_out, s_r_ff_4_q);
  not not_42 (not_42_out, s_r_ff_4_q);
  and and_70 (and_70_out, Read_Addr0_out, Row0_bit3_q);
  and and_71 (and_71_out, Read_Addr0_out, Row0_bit2_q);
  and and_72 (and_72_out, Read_Addr0_out, Row0_bit1_q);
  or or_1 (or_1_out, and_31_out, or_2_out);
  and and_73 (and_73_out, Addr_and_Mode_out, s_r_ff_4_q);
  and and_74 (and_74_out, Addr_and_Mode_out, not_43_out);
  not not_43 (not_43_out, s_r_ff_4_q);
  or or_2 (or_2_out, Read_Addr2_bit0_out, or_4_out);
  and and_75 (and_75_out, Row3_bit3_q, Read_Row3_out);
  and Read_Row3 (Read_Row3_out, Mode_Reg_q, Addr3_And_Gate_out);
  and and_76 (and_76_out, and_9_out, not_38_out);
  and and_77 (and_77_out, Addr4_and_Mode_out, not_44_out);
  not not_44 (not_44_out, s_r_ff_4_q);
  S_R_Flip_Flop Row4_bit0 (.S(and_65_out), .R(and_77_out), .clk(Clck), .Q(Row4_bit0_q));  // open: reset, Qn, preset
  and and_78 (and_78_out, Addr5_and_Mode_out, s_r_ff_4_q);
  not not_45 (not_45_out, s_r_ff_4_q);
  S_R_Flip_Flop Row5_bit0 (.S(and_78_out), .R(and_81_out), .clk(Clck), .Q(Row5_bit0_q));  // open: reset, Qn, preset
  S_R_Flip_Flop Row6_bit0 (.S(and_68_out), .R(and_69_out), .clk(Clck), .Q(Row6_bit0_q));  // open: reset, Qn, preset
  and and_79 (and_79_out, Addr7_and_Mode_out, s_r_ff_4_q);
  S_R_Flip_Flop Row7_bit0 (.S(and_79_out), .R(and_80_out), .clk(Clck), .Q(Row7_bit0_q));  // open: reset, Qn, preset
  and and_80 (and_80_out, Addr7_and_Mode_out, not_42_out);
  or or_3 (or_3_out, and_70_out, or_1_out);
  or or_4 (or_4_out, and_75_out, or_5_out);
  and and_81 (and_81_out, Addr5_and_Mode_out, not_45_out);
  and and_82 (and_82_out, Row6_bit3_q, Addr6_READ_out);
  and Addr6_READ (Addr6_READ_out, Mode_Reg_q, Addr6_And_Gate_out);
  and READ_Addr7 (READ_Addr7_out, Addr7_And_Gate_out, Mode_Reg_q);
  and and_83 (and_83_out, Read_Addr1_out, Row1_bit2_q);
  and and_84 (and_84_out, Row2_bit2_q, Read_Addr2_out);
  or or_5 (or_5_out, and_49_out, or_8_out);
  and READ_Addr7_BIT0 (READ_Addr7_BIT0_out, READ_Addr7_out, Row7_bit3_q);
  or or_6 (or_6_out, and_71_out, or_7_out);
  or or_7 (or_7_out, and_83_out, or_10_out);
  and and_85 (and_85_out, Row3_bit2_q, Read_Row3_out);
  or or_8 (or_8_out, and_52_out, or_9_out);
  and and_86 (and_86_out, Read_Row5_out, Row5_bit2_q);
  or or_9 (or_9_out, and_82_out, READ_Addr7_BIT0_out);
  and and_87 (and_87_out, Addr6_READ_out, Row6_bit2_q);
  and and_88 (and_88_out, READ_Addr7_out, Row7_bit2_q);
  or or_10 (or_10_out, and_84_out, or_14_out);
  and and_89 (and_89_out, Row4_bit2_q, Read_Row4_out);
  or or_11 (or_11_out, and_87_out, and_88_out);
  and and_90 (and_90_out, Read_Row3_out, Row3_bit1_q);
  or or_12 (or_12_out, and_89_out, or_13_out);
  or or_13 (or_13_out, and_86_out, or_11_out);
  and and_91 (and_91_out, Read_Addr1_out, Row1_bit1_q);
  and and_92 (and_92_out, Read_Addr2_out, Row2_bit1_q);
  or or_14 (or_14_out, and_85_out, or_12_out);
  and and_93 (and_93_out, Read_Row4_out, Row4_bit1_q);
  and and_94 (and_94_out, Row5_bit1_q, Read_Row5_out);
  and and_95 (and_95_out, Row6_bit1_q, Addr6_READ_out);
  and and_96 (and_96_out, Row7_bit1_q, READ_Addr7_out);
  or or_15 (or_15_out, and_91_out, or_16_out);
  or or_16 (or_16_out, and_92_out, or_19_out);
  or or_17 (or_17_out, and_94_out, or_18_out);
  or or_18 (or_18_out, and_95_out, and_96_out);
  and and_97 (and_97_out, READ_Addr7_out, Row7_bit0_q);
  and and_98 (and_98_out, Row1_bit0_q, Read_Addr1_out);
  and and_99 (and_99_out, Row2_bit0_q, Read_Addr2_out);
  or or_19 (or_19_out, and_90_out, or_20_out);
  and and_100 (and_100_out, Read_Row3_out, Row3_bit0_q);
  or or_20 (or_20_out, and_93_out, or_17_out);
  and and_101 (and_101_out, Read_Row4_out, Row4_bit0_q);
  and and_102 (and_102_out, Row5_bit0_q, Read_Row5_out);
  and and_103 (and_103_out, Row6_bit0_q, Addr6_READ_out);
  or or_21 (or_21_out, and_72_out, or_15_out);
  or or_22 (or_22_out, and_99_out, or_26_out);
  or or_23 (or_23_out, and_102_out, or_24_out);
  or or_24 (or_24_out, and_103_out, and_97_out);
  or or_25 (or_25_out, and_98_out, or_22_out);
  or or_26 (or_26_out, and_100_out, or_27_out);
  or or_27 (or_27_out, and_101_out, or_23_out);
  or or_28 (or_28_out, and_63_out, or_25_out);
  D_Flip_Flop d_ff_1 (.D(or_3_out), .clk(Clck), .Q(Output_Bit3));  // open: Qn, preset, reset
  D_Flip_Flop d_ff_2 (.D(or_6_out), .clk(Clck), .Q(Output_Bit2));  // open: Qn, preset, reset
  D_Flip_Flop d_ff_3 (.D(or_21_out), .clk(Clck), .Q(Output_Bit1));  // open: Qn, preset, reset
  D_Flip_Flop d_ff_4 (.D(or_28_out), .clk(Clck), .Q(Output_Bit0));  // open: Qn, preset, reset
endmodule

module PC_Incr (
  input  Clck,
  input  One_Bit,
  input  PC0,
  input  PC1,
  input  PC2,
  output PC_Out0,
  output PC_Out1,
  output PC_Out2
);

  wire Carry1, Carry2, d_ff_1_q, d_ff_2_q, d_ff_3_q;

  D_Flip_Flop d_ff_1 (.D(PC0), .clk(Clck), .Q(d_ff_1_q));  // open: Qn, preset, reset
  D_Flip_Flop d_ff_2 (.D(PC1), .clk(Clck), .Q(d_ff_2_q));  // open: Qn, preset, reset
  D_Flip_Flop d_ff_3 (.D(PC2), .clk(Clck), .Q(d_ff_3_q));  // open: Qn, preset, reset
  xor xor_1 (PC_Out0, d_ff_1_q, One_Bit);
  and and_1 (Carry1, d_ff_1_q, One_Bit);
  and and_2 (Carry2, d_ff_2_q, Carry1);
  xor xor_2 (PC_Out1, Carry1, d_ff_2_q);
  xor xor_3 (PC_Out2, Carry2, d_ff_3_q);
endmodule
